# Fritzing sketch weather_station (saved by Fritzing 0.9.3b)
breadboards: 1

parts:
  U1 = atmega168 [package=dip]
  XTAL1 = Crystal [frequency="16 Mhz" package=THT]
  C1 = Ceramic Capacitor [capacitance=18pF package="100 mil [THT, multilayer]"]
  C2 = Ceramic Capacitor [capacitance=18pF package="100 mil [THT, multilayer]"]
  R1 = Resistor [tolerance=±5% resistance=10k package=THT]
  S1 = Pushbutton [package="[THT]"]
  U2 = Voltage Regulator - 5V [package="TO220 [THT]"]
  Power_plug1 = Power plug
  C3 = Electrolytic Capacitor [capacitance=10µF package="100 mil [THT, electrolytic]"]
  C4 = Electrolytic Capacitor [capacitance=10µF package="100 mil [THT, electrolytic]"]
  U3 = Voltage Regulator - 3.3V [package="TO220 [THT]"]
  C5 = Electrolytic Capacitor [capacitance=100nF package="100 mil [THT, electrolytic]"]
  C6 = Electrolytic Capacitor [capacitance=330nF package="100 mil [THT, electrolytic]"]
  LED1 = LED - 5mm [color="Red (633nm)" package="5 mm [THT]"]
  R2 = Resistor [tolerance=±5% resistance=220 package=THT]
  U4 = mystery part, 3 pins [chip_label=LM335]
  R3 = Resistor [tolerance=±5% resistance=4.7k package=THT]
  C7 = Ceramic Capacitor [capacitance=0.1µF package="100 mil [THT, multilayer]"]
  R4 = Resistor [tolerance=±5% resistance=2k package=THT]

nets:
  N1: U1.RESET, R1.Pin_0, S1.Pin_1, S1.Pin_2
  +5V: U1.VCC, U1.AREF, R1.Pin_1, U2.output_voltage, C3.+, LED1.anode, R3.Pin_0, R4.Pin_1
  GND: U1.GND, C1.0, C2.1, S1.Pin_3, S1.Pin_4, R2.Pin_1, U4.pin3, C7.0
  N2: U1.XLAT1, XTAL1.pin_0, C1.1
  N3: U1.XLAT2, XTAL1.pin_1, C2.0
  N4: U1.AVCC, R3.Pin_1, C7.1
  N5: U1.A0, U4.pin2, R4.Pin_0
  N6: U2.input_voltage, Power_plug1.VCC, C4.+, U3.input_voltage, C6.+
  GND_2: U2.GND, Power_plug1.GND, C3.-, C4.-, U3.GND, C5.-, C6.-
  +3,3V: U3.output_voltage, C5.+
  N7: LED1.cathode, R2.Pin_0

notes:
  Power Supply
  LP-Filter
  Controller
  Temp.-Sensor
